// Logisim project LogicalCircuit.circ as structural Verilog: 1 circuit, main circuit main
module main (
  input  X2,
  input  X3,
  input  X4,
  input  X5,
  output Z1,
  output Z2
);

  wire not_1_out, not_2_out, not_3_out, not_4_out, or_1_out, or_2_out, or_3_out, or_4_out, or_5_out,
       or_6_out, or_7_out, or_8_out, or_9_out, or_10_out, or_11_out, or_12_out, or_13_out;

  not not_1 (not_1_out, X2);
  not not_2 (not_2_out, X3);
  not not_3 (not_3_out, X4);
  not not_4 (not_4_out, X5);
  or or_1 (or_1_out, X2, X3, not_3_out, X5);
  or or_2 (or_2_out, X2, not_2_out, X4, not_4_out);
  or or_3 (or_3_out, not_1_out, X3, X4, X5);
  or or_4 (or_4_out, not_1_out, X3, not_3_out, X5);
  or or_5 (or_5_out, not_1_out, not_2_out, not_3_out, X5);
  or or_6 (or_6_out, not_1_out, not_2_out, not_3_out, not_4_out);
  or or_7 (or_7_out, X2, X3, X4, X5);
  or or_8 (or_8_out, X2, X3, X4, not_4_out);
  or or_9 (or_9_out, X2, not_2_out, X4, not_4_out);
  or or_10 (or_10_out, X2, not_2_out, not_3_out, not_4_out);
  or or_11 (or_11_out, not_1_out, X3, X4, not_4_out);
  or or_12 (or_12_out, not_1_out, X3, not_3_out, not_4_out);
  or or_13 (or_13_out, not_1_out, not_2_out, X4, not_4_out);
  and and_1 (Z1, or_1_out, or_2_out, or_3_out, or_4_out, or_5_out, or_6_out);
  and and_2 (Z2, or_7_out, or_8_out, or_9_out, or_10_out, or_11_out, or_12_out, or_13_out);
endmodule
