// Logisim project OptimizedCircuit.circ as structural Verilog: 1 circuit, main circuit main
module main (
  input  in_1,
  input  in_2,
  input  in_3,
  input  in_4,
  input  in_5,
  input  in_6,
  input  in_7,
  input  in_8,
  output out_9,
  output out_10
);

  wire not_1_out, not_2_out, not_3_out, not_4_out, not_5_out, not_6_out, or_1_out, or_2_out, or_3_out,
       or_4_out, or_5_out, or_6_out, or_7_out, or_8_out;

  not not_1 (not_1_out, in_1);
  not not_2 (not_2_out, in_2);
  not not_3 (not_3_out, in_6);
  not not_4 (not_4_out, in_3);
  not not_5 (not_5_out, in_4);
  not not_6 (not_6_out, in_8);
  or or_1 (or_1_out, in_1, not_2_out, in_3, not_5_out);
  or or_2 (or_2_out, not_1_out, not_2_out, not_4_out);
  or or_3 (or_3_out, not_1_out, in_2, in_4);
  or or_4 (or_4_out, in_2, not_4_out, in_4);
  or or_5 (or_5_out, in_5, in_6, in_7);
  or or_6 (or_6_out, in_7, not_6_out);
  or or_7 (or_7_out, in_5, not_3_out, not_6_out);
  or or_8 (or_8_out, not_3_out, in_7, not_6_out);
  and and_1 (out_9, or_1_out, or_2_out, or_3_out, or_4_out);
  and and_2 (out_10, or_5_out, or_6_out, or_7_out, or_8_out);
endmodule
