// Logisim project adder01010101.circ as structural Verilog: 2 circuits, main circuit main
module main (
  input  [3:0] NegativeB,
  input  [3:0] A0,
  input  [3:0] B0,
  input  [3:0] A1,
  input  [3:0] B1,
  input  [3:0] A2,
  input  [3:0] B2,
  input  [3:0] A3,
  input  [3:0] B3,
  output [3:0] out_10,
  output [3:0] out_11,
  output [3:0] out_12,
  output [3:0] out_13,
  output [3:0] out_14
);

  wire [3:0] undriven, undriven_2, undriven_3, xor_1_out, xor_2_out, xor_3_out, xor_4_out;

  assign xor_1_out = NegativeB ^ B0;  // XOR_Gate xor_1, 4 bits wide
  assign xor_2_out = NegativeB ^ B1;  // XOR_Gate xor_2, 4 bits wide
  assign xor_3_out = NegativeB ^ B2;  // XOR_Gate xor_3, 4 bits wide
  assign xor_4_out = NegativeB ^ B3;  // XOR_Gate xor_4, 4 bits wide
  Adders adders_1 (.in_1(NegativeB), .in_2(A0), .in_3(xor_1_out), .out_4(out_10));
  Adders adders_2 (.in_1(undriven), .in_2(A1), .in_3(xor_2_out), .out_4(out_11));
  Adders adders_3 (.in_1(undriven_2), .in_2(A2), .in_3(xor_3_out), .out_4(out_12));
  Adders adders_4 (.in_1(undriven_3), .in_2(A3), .in_3(xor_4_out), .out_4(out_13));
endmodule

module Adders (
  input  [3:0] in_1,
  input  [3:0] in_2,
  input  [3:0] in_3,
  output [3:0] out_4
);

  wire [3:0] and_1_out, and_2_out, or_1_out, undriven, undriven_2, undriven_3, xor_1_out;

  assign or_1_out = and_1_out | and_2_out;  // OR_Gate or_1, 4 bits wide
  assign and_1_out = undriven & undriven_2;  // AND_Gate and_1, 4 bits wide
  assign and_2_out = xor_1_out & undriven_3;  // AND_Gate and_2, 4 bits wide
  xor xor_1 (xor_1_out[0], undriven[0], undriven_2[0]);
  // XOR_Gate xor_2 has open pins: in0=xor_1_out[0], in1=undriven_3[0], out=open
  // Pins of 1 and 4 bits meet at xor_1_out
  // Pins of 1 and 4 bits meet at undriven
  // Pins of 1 and 4 bits meet at undriven_2
  // Pins of 1 and 4 bits meet at undriven_3
endmodule
